// Logisim project REGARRAY.circ as structural Verilog: 1 circuit, main circuit main
// 2
module main (
  input  [15:0] Data,
  input  [3:0] Read0,
  input  [3:0] Read1,
  input  [3:0] Write0,
  input  WritePerm,
  input  Clock,
  input  [6:0] in_7,
  output [15:0] out_8,
  output [15:0] out_9,
  output out_10
);

  wire and_1_out, and_2_out, and_3_out, and_4_out, comparator_1_eq, comparator_2_eq, decoder_1_out0,
       decoder_1_out1, decoder_1_out2, decoder_1_out3;
  wire [7:0] random_1_out;
  wire [15:0] bit_extender_1_out, bit_extender_2_out, register_1_q, register_2_q, register_3_q, register_4_q,
       register_5_q, register_6_q;

  Comparator #(.width(4)) comparator_1 (.a(4'b0100), .b(Read0), .eq(comparator_1_eq));  // open: gt, lt
  Comparator #(.width(4)) comparator_2 (.a(Read1), .b(4'b0100), .eq(comparator_2_eq));  // open: gt, lt
  or or_1 (out_10, comparator_1_eq, comparator_2_eq);
  Decoder #(.select(4), .enable("false")) decoder_1 (
    .out0(decoder_1_out0), .out1(decoder_1_out1), .out2(decoder_1_out2), .out3(decoder_1_out3), .sel(Write0));  // open: out4, out5, out6, out7, out8, out9, out10, out11, out12, out13, out14, out15
  and and_1 (and_1_out, WritePerm, decoder_1_out0);
  and and_2 (and_2_out, WritePerm, decoder_1_out1);
  and and_3 (and_3_out, WritePerm, decoder_1_out2);
  and and_4 (and_4_out, WritePerm, decoder_1_out3);
  assign bit_extender_1_out = {{9{1'b0}}, in_7};  // Bit_Extender bit_extender_1
  Random random_1 (.clk(Clock), .next(1'b1), .out(random_1_out));  // open: clr
  assign bit_extender_2_out = {{8{1'b0}}, random_1_out};  // Bit_Extender bit_extender_2
  Register #(.width(16)) register_1 (.D(Data), .en(and_1_out), .Q(register_1_q), .clk(Clock));  // open: clr
  Register #(.width(16)) register_2 (.D(Data), .en(and_2_out), .Q(register_2_q), .clk(Clock));  // open: clr
  Register #(.width(16)) register_3 (.D(Data), .en(and_3_out), .Q(register_3_q), .clk(Clock));  // open: clr
  Register #(.width(16)) register_4 (.D(Data), .en(and_4_out), .Q(register_4_q), .clk(Clock));  // open: clr
  Register #(.width(16)) register_5 (.D(bit_extender_1_out), .en(out_10), .Q(register_5_q), .clk(Clock));  // open: clr
  Register #(.width(16)) register_6 (.D(bit_extender_2_out), .en(1'b1), .Q(register_6_q), .clk(Clock));  // open: clr
  Multiplexer #(.select(4), .width(16), .enable("false")) multiplexer_1 (
    .in0(register_1_q), .in1(register_2_q), .in2(register_3_q), .in3(register_4_q), .in4(register_5_q),
    .in5(register_6_q), .out(out_8), .sel(Read0));  // open: in6, in7, in8, in9, in10, in11, in12, in13, in14, in15
  Multiplexer #(.select(4), .width(16), .enable("false")) multiplexer_2 (
    .in0(register_1_q), .in1(register_2_q), .in2(register_3_q), .in3(register_4_q), .in4(register_5_q),
    .in5(register_6_q), .out(out_9), .sel(Read1));  // open: in6, in7, in8, in9, in10, in11, in12, in13, in14, in15
endmodule
